# Fritzing sketch Project (saved by Fritzing 0.9.3b)
breadboards: 2

parts:
  U1 = NodeMCU V3.0
  Part1 = Soil Moisture Sensor
  YL-83_-_Control_Board1 = YL-83 Rain Sensor - Control Board

nets:
  3V3: U1.3V3, YL-83_-_Control_Board1.VCC
  N1: U1.GND#6, U1.GND#13, U1.GND#16, U1.GND#33, YL-83_-_Control_Board1.GND
  N2: U1.A0, YL-83_-_Control_Board1.AO
  N3: Part1.GND, YL-83_-_Control_Board1.NEG
  N4: Part1.VCC, YL-83_-_Control_Board1.POS

custom parts:
  NodeMCU V3.0: ESP8266 based NodeMCU
  YL-83 Rain Sensor - Control Board: The YL-83 is a rain sensor that has more resistance when dry and less resistance when wet. The module runs at 5V.
